// Logisim project lab1.4.circ as structural Verilog: 1 circuit, main circuit main
module main (
  input  D0,
  input  D1,
  input  S,
  output Y
);


  // Notes on the sheet:
  //   输入引脚
  //   请勿修改引脚名称及电路封装外观
  //   提示：使用传输门和晶体管来实现二选一多路选择器，禁止直接使用选择器组件。
  //   输出引脚
endmodule
