// Logisim project lab1.5.circ as structural Verilog: 2 circuits, main circuit 4-1MUX
module _4_1MUX (
  input  D0,
  input  D1,
  input  D2,
  input  D3,
  input  S0,
  input  S1,
  output Y
);


  // Notes on the sheet:
  //   输入引脚
  //   请勿修改引脚名称、电路名称及电路封装外观
  //   提示：使用二选一多路选择器子电路级联实现四选一多路选择器，禁止直接使用多路选择器组件。
  //   输出引脚
endmodule

module _2_1MUX (
  input  D0,
  input  D1,
  input  S,
  output Y
);


  // Notes on the sheet:
  //   输入引脚
  //   请勿修改引脚名称及电路封装外观
  //   提示：使用传输门和晶体管来实现二选一多路选择器，禁止直接使用选择器组件。
  //   输出引脚
endmodule
