// Logisim project lab2.4.circ as structural Verilog: 3 circuits, main circuit main
module main (
  input  [6:0] Input,
  output [6:0] Output,
  output NoError
);

  wire \n3_8译码器_1_y0_l , \n3_8译码器_1_y1_l , \n3_8译码器_1_y2_l , \n3_8译码器_1_y3_l , \n3_8译码器_1_y4_l ,
       \n3_8译码器_1_y5_l , \n3_8译码器_1_y6_l , \n3_8译码器_1_y7_l , \n4位奇偶校验器_1_odd , \n4位奇偶校验器_2_odd ,
       \n4位奇偶校验器_3_odd , not_1_out, not_3_out, not_4_out, not_5_out, not_6_out, not_7_out, not_8_out,
       not_9_out;

  \_4位奇偶校验器  \u_4位奇偶校验器_1  (
    .N0(Input[6]), .N1(Input[4]), .N2(Input[2]), .N3(Input[0]), .ODD(\n4位奇偶校验器_1_odd ));  // open: EVEN
  \_4位奇偶校验器  \u_4位奇偶校验器_2  (
    .N0(Input[6]), .N1(Input[5]), .N2(Input[2]), .N3(Input[1]), .ODD(\n4位奇偶校验器_2_odd ));  // open: EVEN
  \_4位奇偶校验器  \u_4位奇偶校验器_3  (
    .N0(Input[6]), .N1(Input[5]), .N2(Input[4]), .N3(Input[3]), .ODD(\n4位奇偶校验器_3_odd ));  // open: EVEN
  not not_1 (not_1_out, 1'b0);
  not not_2 (NoError, \n3_8译码器_1_y0_l );
  not not_3 (not_3_out, \n3_8译码器_1_y1_l );
  \_3_8译码器  \u_3_8译码器_1  (
    .G1(not_1_out), .G2A_L(1'b0), .G2B_L(1'b0), .Y0_L(\n3_8译码器_1_y0_l ), .Y1_L(\n3_8译码器_1_y1_l ),
    .Y2_L(\n3_8译码器_1_y2_l ), .A(\n4位奇偶校验器_1_odd ), .B(\n4位奇偶校验器_2_odd ), .C(\n4位奇偶校验器_3_odd ),
    .Y3_L(\n3_8译码器_1_y3_l ), .Y4_L(\n3_8译码器_1_y4_l ), .Y5_L(\n3_8译码器_1_y5_l ), .Y6_L(\n3_8译码器_1_y6_l ),
    .Y7_L(\n3_8译码器_1_y7_l ));
  not not_4 (not_4_out, \n3_8译码器_1_y2_l );
  not not_5 (not_5_out, \n3_8译码器_1_y3_l );
  not not_6 (not_6_out, \n3_8译码器_1_y4_l );
  not not_7 (not_7_out, \n3_8译码器_1_y5_l );
  not not_8 (not_8_out, \n3_8译码器_1_y6_l );
  not not_9 (not_9_out, \n3_8译码器_1_y7_l );
  xor xor_1 (Output[0], Input[0], not_3_out);
  xor xor_2 (Output[1], Input[1], not_4_out);
  xor xor_3 (Output[2], Input[2], not_5_out);
  xor xor_4 (Output[3], Input[3], not_6_out);
  xor xor_5 (Output[4], Input[4], not_7_out);
  xor xor_6 (Output[5], Input[5], not_8_out);
  xor xor_7 (Output[6], Input[6], not_9_out);
  Hex_Digit_Display hex_digit_display_1 ();  // open: value, dp

  // Notes on the sheet:
  //   输入引脚
  //   输入引脚
  //   请勿修改引脚名称、电路名称及电路封装外观
  //   提示：使用异或门、4位奇偶校验电路和74x138子电路实现7位汉明码纠错电路。
  //   输出引脚
endmodule

module \_3_8译码器  (
  input  G1,
  input  G2A_L,
  input  G2B_L,
  input  A,
  input  B,
  input  C,
  output Y0_L,
  output Y1_L,
  output Y2_L,
  output Y3_L,
  output Y4_L,
  output Y5_L,
  output Y6_L,
  output Y7_L
);

  wire and_1_out, not_1_out, not_2_out, not_3_out, not_4_out, not_5_out, not_6_out, not_7_out;

  not not_1 (not_1_out, G1);
  and and_1 (and_1_out, ~not_1_out, ~G2A_L, ~G2B_L);  // AND_Gate
  not not_2 (not_2_out, A);
  not not_3 (not_3_out, not_2_out);
  not not_4 (not_4_out, not_5_out);
  not not_5 (not_5_out, B);
  not not_6 (not_6_out, C);
  not not_7 (not_7_out, not_6_out);
  nand nand_1 (Y0_L, not_2_out, not_5_out, not_6_out, and_1_out);
  nand nand_2 (Y1_L, not_5_out, not_6_out, not_3_out, and_1_out);
  nand nand_3 (Y2_L, not_2_out, not_6_out, not_4_out, and_1_out);
  nand nand_4 (Y3_L, not_6_out, not_3_out, not_4_out, and_1_out);
  nand nand_5 (Y4_L, not_2_out, not_5_out, not_7_out, and_1_out);
  nand nand_6 (Y5_L, not_5_out, not_3_out, not_7_out, and_1_out);
  nand nand_7 (Y6_L, not_2_out, not_4_out, not_7_out, and_1_out);
  nand nand_8 (Y7_L, and_1_out, not_4_out, not_7_out, not_3_out);

  // Notes on the sheet:
  //   输入引脚
  //   3-8译码器
  //   请勿修改引脚名称、电路名称及电路封装外观
  //   提示：使用独立逻辑门实现3-8译码器，禁止直接使用译码器组件。
  //   输出引脚
endmodule

module \_4位奇偶校验器  (
  input  N0,
  input  N1,
  input  N2,
  input  N3,
  output EVEN,
  output ODD
);

  ExactlyOne xor_1 (.out(ODD), .in0(N0), .in1(N1), .in2(N2), .in3(N3));
  not not_1 (EVEN, ODD);

  // Notes on the sheet:
  //   4位奇偶校验电路
endmodule
