// Logisim project test.circ as structural Verilog: 2 circuits, main circuit main
module main (
  input  in_1,
  input  in_2,
  input  in_3,
  input  in_4,
  input  in_5,
  input  in_6
);

  wire G;

  Multiplexer #(.select(2), .enable("false")) multiplexer_1 (
    .in0(in_1), .in1(in_2), .in2(in_3), .in3(in_4), .out(G), .sel({in_6, in_5}));

  // Other names for the same wires on the sheet: F = in_5; E = in_6; A = in_1; B = in_2; C = in_3; D = in_4
endmodule

module \特色  (
  input  in_1,
  input  in_2
);

  wire and_1_out;

  and and_1 (and_1_out, in_1, in_2);
endmodule
